# Fritzing sketch fritzingMainBoardSchematic (saved by Fritzing 0.9.9b)

parts:
  IRFZ44N = Basic FET N-Channel [package="TO220 [THT]"]
  Q2 = Basic FET N-Channel [package="TO220 [THT]"]
  ESP32_DevBoard_(dual_core) = MH-ET LIVE ESP32 DEVKIT 38 pins
  80mm_24V_Fan = Fan - Ventilador [package=THT]
  24V_to_9V_step_down_converter = RioRand LM2596
  7805 = Voltage Regulator - 5V [package="DPak [SMD]"]
  UART_to_RS485_module = RS485_XY-017 [part_number=XY-017]
  TC4420 = TC4420 [package=dil-08]
  DMX_IN = XLR NC3MAAH [package=nc3maah]
  C1_330nF = Capacitor [package=cap-pth-small2]
  C2_100nf = Capacitor [package=cap-pth-small2]
  R1 = Resistor [package=THT]
  R2 = Resistor [package=THT]
  R3 = Resistor [package=THT]
  R4 = Resistor [package=THT]
  R5 = Resistor [package=THT]
  Fan_indicator_LED = LED - 5mm [color="Red (633nm)" package="5 mm [THT]"]
  R6 = Resistor [package=THT]
  Strobe_indicator_LED = LED - 5mm [color="Red (633nm)" package="5 mm [THT]"]
  R7 = Resistor [package=THT]
  24V_IN = Screw terminal - 2 pins [package=THT]
  Strobe_LED_GND = Screw terminal - 2 pins [package=THT]

nets:
  N1: IRFZ44N.gate, TC4420.OUTPUT#5
  N2: IRFZ44N.drain, Strobe_LED_GND.pin2
  N3: IRFZ44N.source, Strobe_LED_GND.pin1
  N4: Q2.gate, R3.Pin_0, R5.Pin_0
  N5: Q2.drain, 80mm_24V_Fan.GND, R6.Pin_0
  N6: Q2.source, 24V_to_9V_step_down_converter.Pin_2, R5.Pin_1, 24V_IN.pin1
  N7: ESP32_DevBoard_(dual_core).IO25, TC4420.INPUT, R4.Pin_1
  N8: ESP32_DevBoard_(dual_core).IO26, R3.Pin_1
  N9: ESP32_DevBoard_(dual_core).CMD, 24V_to_9V_step_down_converter.Pin_4, 7805.GND, UART_to_RS485_module.GND#0, TC4420.GND#3, C1_330nF.1, C2_100nf.2, R2.Pin_0
  5V: ESP32_DevBoard_(dual_core).5V, 24V_to_9V_step_down_converter.Pin_3, 7805.input_voltage, TC4420.VDD, C1_330nF.2
  N10: ESP32_DevBoard_(dual_core).IO16, UART_to_RS485_module.TXD, R1.Pin_0, R2.Pin_1
  N11: 80mm_24V_Fan.24v, 24V_to_9V_step_down_converter.Pin_1, Fan_indicator_LED.anode, 24V_IN.pin2
  N12: 7805.output_voltage, UART_to_RS485_module.VCC, C2_100nf.1, R1.Pin_1
  N13: UART_to_RS485_module.A, DMX_IN.3
  N14: UART_to_RS485_module.B, DMX_IN.2
  N15: UART_to_RS485_module.GND#5, DMX_IN.1
  N16: TC4420.GND#4, R4.Pin_0, Strobe_indicator_LED.cathode
  N17: TC4420.OUTPUT#6, R7.Pin_1
  N18: Fan_indicator_LED.cathode, R6.Pin_1
  N19: Strobe_indicator_LED.anode, R7.Pin_0

custom parts:
  MH-ET LIVE ESP32 DEVKIT 38 pins: http://mh.nodebb.com/topic/2/mh-et-live-esp32-devkit
  Fan - Ventilador: Ventilador de 2 pines, se encuentra comunmente en computadoras de escritorio
  RS485_XY-017: Commercially available RS485 to RS232 TTL Module
  TC4420: 6A High-Speed MOSFET Driver
  Resistor: A generic 5-band resistor (0.25W)
  Resistor: A generic 5-band resistor (0.25W)
  Resistor: A generic 5-band resistor (0.25W)
  Resistor: A generic 5-band resistor (0.25W)
  Resistor: A generic 5-band resistor (0.25W)
  Resistor: A generic 5-band resistor (0.25W)
